// Logisim project aula 1.circ as structural Verilog: 2 circuits, main circuit main
module main (
  input  in_1,
  input  in_2,
  input  in_3,
  output out_4,
  output out_5
);

  wire and_1_out, and_2_out, and_3_out, xor_1_out;

  xor xor_1 (xor_1_out, in_2, in_1);
  and and_1 (and_1_out, in_2, in_1);
  and and_2 (and_2_out, in_2, in_1);
  and and_3 (and_3_out, in_1, in_1);
  xor xor_2 (out_4, xor_1_out, in_1);
  or or_1 (out_5, and_1_out, and_2_out, and_3_out);

  assign in_3 = in_1;
endmodule

module circuitoSomador (
  input  in_1,
  input  in_2
);
endmodule
