// Logisim project aula3.circ as structural Verilog: 7 circuits, main circuit main
module main (
  input  [7:0] input1,
  input  [7:0] in_2,
  input  [7:0] in_3,
  input  set,
  input  in_5,
  input  in_6,
  input  in_7,
  input  in_8,
  input  in_9,
  input  in_10,
  input  in_11,
  input  [7:0] in_12,
  input  write,
  input  eneable,
  output [7:0] out_15,
  output out_16,
  output out_17,
  output out_18,
  output out_19
);

  wire and_1_out, decoder_1_out0, decoder_1_out1, decoder_1_out2, decoder_1_out3, decoder_1_out4,
       decoder_1_out5, decoder_1_out6, decoder_1_out7, decoder_1_out8, decoder_1_out9, decoder_1_out10,
       decoder_1_out11, decoder_1_out12, decoder_1_out13, decoder_1_out14, decoder_1_out15, decoder_2_out0,
       decoder_2_out1, decoder_2_out2, decoder_2_out3, decoder_2_out4, decoder_2_out5, decoder_2_out6,
       decoder_2_out7, decoder_2_out8, decoder_2_out9, decoder_2_out10, decoder_2_out11, decoder_2_out12,
       decoder_2_out13, decoder_2_out14, decoder_2_out15;
  wire [7:0] registrador_8bits_1_out_3, registrador_8bits_2_out_3, registrador_8bits_3_out_3;

  deco_2x4 deco_2x4_1 (.in_1(in_10), .in_2(in_11), .out_3(out_16), .out_4(out_17), .out_5(out_18), .out_6(out_19));
  // Probe on out_15
  // Probe on registrador_8bits_1_out_3
  registrador_8bits registrador_8bits_1 (.in_1(input1), .in_2(set), .out_3(registrador_8bits_1_out_3));
  enable enable_1 (.in_1(registrador_8bits_1_out_3), .in_2(in_7), .out_3(out_15));
  Decoder #(.enable("false"), .select(4)) decoder_1 (
    .out0(decoder_1_out0), .out1(decoder_1_out1), .out2(decoder_1_out2), .out3(decoder_1_out3),
    .out4(decoder_1_out4), .out5(decoder_1_out5), .out6(decoder_1_out6), .out7(decoder_1_out7),
    .out8(decoder_1_out8), .out9(decoder_1_out9), .out10(decoder_1_out10), .out11(decoder_1_out11),
    .out12(decoder_1_out12), .out13(decoder_1_out13), .out14(decoder_1_out14), .out15(decoder_1_out15),
    .sel(in_12[7:4]));
  enable enable_2 (.in_1(registrador_8bits_2_out_3), .in_2(in_8), .out_3(out_15));
  // Probe on registrador_8bits_2_out_3
  registrador_8bits registrador_8bits_2 (.in_1(in_2), .in_2(in_5), .out_3(registrador_8bits_2_out_3));
  Decoder #(.enable("false"), .select(4)) decoder_2 (
    .out0(decoder_2_out0), .out1(decoder_2_out1), .out2(decoder_2_out2), .out3(decoder_2_out3),
    .out4(decoder_2_out4), .out5(decoder_2_out5), .out6(decoder_2_out6), .out7(decoder_2_out7),
    .out8(decoder_2_out8), .out9(decoder_2_out9), .out10(decoder_2_out10), .out11(decoder_2_out11),
    .out12(decoder_2_out12), .out13(decoder_2_out13), .out14(decoder_2_out14), .out15(decoder_2_out15),
    .sel(in_12[3:0]));
  enable enable_3 (.in_1(registrador_8bits_3_out_3), .in_2(in_9), .out_3(out_15));
  // Probe on registrador_8bits_3_out_3
  registrador_8bits registrador_8bits_3 (.in_1(in_3), .in_2(in_6), .out_3(registrador_8bits_3_out_3));
  and and_1 (and_1_out, decoder_1_out0, decoder_2_out0);
  // AND_Gate and_2 has open pins: in0=and_1_out, in1=write, out=open
  // AND_Gate and_3 has open pins: in0=and_1_out, in1=eneable, out=open

  // Other names for the same wires on the sheet: oe = eneable; we = write
endmodule

module registrador_8bits (
  input  [7:0] in_1,
  input  in_2,
  output [7:0] out_3
);

  memoria_um_bit memoria_um_bit_1 (.in_1(in_1[0]), .in_2(in_2), .out_3(out_3[0]));
  memoria_um_bit memoria_um_bit_2 (.in_1(in_1[1]), .in_2(in_2), .out_3(out_3[1]));
  memoria_um_bit memoria_um_bit_3 (.in_1(in_1[2]), .in_2(in_2), .out_3(out_3[2]));
  memoria_um_bit memoria_um_bit_4 (.in_1(in_1[3]), .in_2(in_2), .out_3(out_3[3]));
  memoria_um_bit memoria_um_bit_5 (.in_1(in_1[4]), .in_2(in_2), .out_3(out_3[4]));
  memoria_um_bit memoria_um_bit_6 (.in_1(in_1[5]), .in_2(in_2), .out_3(out_3[5]));
  memoria_um_bit memoria_um_bit_7 (.in_1(in_1[6]), .in_2(in_2), .out_3(out_3[6]));
  memoria_um_bit memoria_um_bit_8 (.in_1(in_1[7]), .in_2(in_2), .out_3(out_3[7]));
endmodule

module memoria_um_bit (
  input  in_1,
  input  in_2,
  output out_3
);

  wire nand_1_out, nand_2_out, nand_4_out;

  nand nand_1 (nand_1_out, in_1, in_2);
  nand nand_2 (nand_2_out, nand_1_out, in_2);
  nand nand_3 (out_3, nand_1_out, nand_4_out);
  nand nand_4 (nand_4_out, out_3, nand_2_out);
endmodule

module enable (
  input  [7:0] in_1,
  input  in_2,
  output [7:0] out_3
);

  wire [7:0] and_1_out;

  and and_1 (and_1_out[0], in_1[0], in_2);
  and and_2 (and_1_out[1], in_1[1], in_2);
  and and_3 (and_1_out[2], in_1[2], in_2);
  and and_4 (and_1_out[3], in_1[3], in_2);
  and and_5 (and_1_out[4], in_1[4], in_2);
  and and_6 (and_1_out[5], in_1[5], in_2);
  and and_7 (and_1_out[6], in_1[6], in_2);
  and and_8 (and_1_out[7], in_1[7], in_2);
  assign out_3 = in_2 ? and_1_out : 8'bz;  // Controlled_Buffer controlled_buffer_1
endmodule

module deco_2x4 (
  input  in_1,
  input  in_2,
  output out_3,
  output out_4,
  output out_5,
  output out_6
);

  wire not_1_out, not_2_out;

  not not_1 (not_1_out, in_1);
  not not_2 (not_2_out, in_2);
  and and_1 (out_3, not_1_out, not_2_out);
  and and_2 (out_4, not_2_out, in_1);
  and and_3 (out_5, not_1_out, in_2);
  and and_4 (out_6, in_1, in_2);
endmodule

module registrador (
  input  [7:0] in_1,
  input  in_2,
  input  in_3,
  output [7:0] out_4
);

  wire [7:0] memoria_um_bit_1_out_3;

  memoria_um_bit memoria_um_bit_1 (.in_1(in_1[0]), .in_2(in_2), .out_3(memoria_um_bit_1_out_3[0]));
  memoria_um_bit memoria_um_bit_2 (.in_1(in_1[1]), .in_2(in_2), .out_3(memoria_um_bit_1_out_3[1]));
  memoria_um_bit memoria_um_bit_3 (.in_1(in_1[2]), .in_2(in_2), .out_3(memoria_um_bit_1_out_3[2]));
  memoria_um_bit memoria_um_bit_4 (.in_1(in_1[3]), .in_2(in_2), .out_3(memoria_um_bit_1_out_3[3]));
  memoria_um_bit memoria_um_bit_5 (.in_1(in_1[4]), .in_2(in_2), .out_3(memoria_um_bit_1_out_3[4]));
  memoria_um_bit memoria_um_bit_6 (.in_1(in_1[5]), .in_2(in_2), .out_3(memoria_um_bit_1_out_3[5]));
  memoria_um_bit memoria_um_bit_7 (.in_1(in_1[6]), .in_2(in_2), .out_3(memoria_um_bit_1_out_3[6]));
  memoria_um_bit memoria_um_bit_8 (.in_1(in_1[7]), .in_2(in_2), .out_3(memoria_um_bit_1_out_3[7]));
  assign out_4 = in_3 ? memoria_um_bit_1_out_3 : 8'bz;  // Controlled_Buffer controlled_buffer_1
endmodule

module ramAula3 (
  input  [7:0] in_1,
  input  in_2,
  input  in_3,
  input  in_4,
  input  [7:0] in_5,
  input  in_6,
  input  in_7,
  input  in_8,
  input  in_9
);

  wire or_1_out;
  wire [7:0] mar_q, registrador_1_out_4;

  // Probe on registrador_1_out_4
  registrador registrador_1 (.in_1(in_1), .in_2(in_3), .in_3(in_4), .out_4(registrador_1_out_4));
  registrador registrador_2 (.in_1(in_5), .in_2(in_6), .in_3(in_7), .out_4(registrador_1_out_4));
  or or_1 (or_1_out, in_8, in_9);
  Register mar (.D(registrador_1_out_4), .Q(mar_q), .clk(in_2));  // open: en, clr
  RAM #(.databus("bidir")) ram_1 (.addr(mar_q), .we(in_8), .oe(in_9), .clk(or_1_out));  // open: data
endmodule
